# Fritzing sketch project_sketch (saved by Fritzing 0.9.3b)
breadboards: 1

parts:
  J1 = Piezo Speaker
  Часть1 = Arduino Mega 2560 (Rev3)
  S1 = Pushbutton [package="[THT]"]
  S2 = Pushbutton [package="[THT]"]
  S3 = Pushbutton [package="[THT]"]
  R1 = Resistor [tolerance=±5% resistance=220 package=THT]

nets:
  N1: J1.pin1, Часть1.D2_PWM
  N2: J1.pin2, Часть1.GND, S1.Pin_3, S1.Pin_4, S2.Pin_1, S2.Pin_2, S3.Pin_1, S3.Pin_2, R1.Pin_0
  N3: Часть1.D3_PWM, S1.Pin_1, S1.Pin_2
  N4: Часть1.D4_PWM, S2.Pin_3, S2.Pin_4
  N5: Часть1.D5_PWM, S3.Pin_3, S3.Pin_4
